// Logisim project 16bitreg.circ as structural Verilog: 2 circuits, main circuit main
module main (
);

  _16_bit_reg u_16_bit_reg_1 ();  // open: Data_In, Read_Address__rs, RegWrite, CLK, Write_Address_rd, Read_Address_2_rt, out_7, Data_2
endmodule

module _16_bit_reg (
  input  [15:0] Data_In,
  input  [1:0] Read_Address__rs,
  input  [1:0] Write_Address_rd,
  input  [1:0] Read_Address_2_rt,
  input  RegWrite,
  input  CLK,
  output [15:0] out_7,
  output [15:0] Data_2
);

  wire and_1_out, and_2_out, and_3_out, and_4_out, decoder_1_out0, decoder_1_out1, decoder_1_out2,
       decoder_1_out3;
  wire [15:0] register_1_q, register_2_q, register_3_q, register_4_q;

  Decoder #(.select(2), .enable("false")) decoder_1 (
    .out0(decoder_1_out0), .out1(decoder_1_out1), .out2(decoder_1_out2), .out3(decoder_1_out3),
    .sel(Write_Address_rd));
  and and_1 (and_1_out, decoder_1_out0, RegWrite);
  and and_2 (and_2_out, decoder_1_out1, RegWrite);
  and and_3 (and_3_out, decoder_1_out2, RegWrite);
  and and_4 (and_4_out, decoder_1_out3, RegWrite);
  Register #(.width(16)) register_1 (.D(Data_In), .en(and_1_out), .Q(register_1_q), .clk(CLK));  // open: clr
  Register #(.width(16)) register_2 (.D(Data_In), .en(and_2_out), .Q(register_2_q), .clk(CLK));  // open: clr
  Register #(.width(16)) register_3 (.D(Data_In), .en(and_3_out), .Q(register_3_q), .clk(CLK));  // open: clr
  Register #(.width(16)) register_4 (.D(Data_In), .en(and_4_out), .Q(register_4_q), .clk(CLK));  // open: clr
  Multiplexer #(.select(2), .width(16)) multiplexer_1 (
    .in0(register_1_q), .in1(register_2_q), .in2(register_3_q), .in3(register_4_q), .out(out_7),
    .sel(Read_Address__rs));  // open: en
  Multiplexer #(.select(2), .width(16)) multiplexer_2 (
    .in0(register_1_q), .in1(register_2_q), .in2(register_3_q), .in3(register_4_q), .out(Data_2),
    .sel(Read_Address_2_rt));  // open: en
endmodule
