// Logisim project 1st Circuit.circ as structural Verilog: 3 circuits, main circuit main
module main (
);

  wire undriven_5, undriven_6;
  wire [3:0] undriven_2, undriven_3, undriven_4;
  wire [15:0] Data_In_out_7, Data_In_out_8, undriven;

  _16bit_Register_File Data_In (
    .DAta_In(undriven), .out_7(Data_In_out_7), .out_8(Data_In_out_8), .Data_Address__rd(undriven_4),
    .Register_Weite(undriven_5), .Clock(undriven_6), .Read_Address_1_rs(undriven_2),
    .Read_Address_2_rt(undriven_3));
endmodule

module _16bit_Reg_File (
  input  [15:0] DAta_In,
  input  [1:0] Read_Address_1_rs,
  input  [1:0] Data_Address__rd,
  input  [1:0] Read_Address_2_rt,
  input  in_5,
  input  Reg_Write,
  output [15:0] out_7,
  output [15:0] out_8
);

  wire decoder_1_out0, decoder_1_out1, decoder_1_out2, decoder_1_out3;
  wire [15:0] register_1_q, register_2_q, register_3_q, register_4_q;

  Decoder #(.select(2)) decoder_1 (
    .out0(decoder_1_out0), .out1(decoder_1_out1), .out2(decoder_1_out2), .out3(decoder_1_out3),
    .sel(Data_Address__rd));  // open: en
  Register #(.width(16)) register_1 (.D(DAta_In), .en(decoder_1_out0), .Q(register_1_q), .clk(in_5));  // open: clr
  Register #(.width(16)) register_2 (.D(DAta_In), .en(decoder_1_out1), .Q(register_2_q), .clk(in_5));  // open: clr
  Register #(.width(16)) register_3 (.D(DAta_In), .en(decoder_1_out2), .Q(register_3_q), .clk(in_5));  // open: clr
  Register #(.width(16)) register_4 (.D(DAta_In), .en(decoder_1_out3), .Q(register_4_q), .clk(in_5));  // open: clr
  Multiplexer #(.select(2), .width(16)) multiplexer_1 (
    .in0(register_1_q), .in1(register_2_q), .in2(register_3_q), .in3(register_4_q), .out(out_7),
    .sel(Read_Address_1_rs));  // open: en
  Multiplexer #(.select(2), .width(16)) multiplexer_2 (
    .in0(register_1_q), .in1(register_2_q), .in2(register_3_q), .in3(register_4_q), .out(out_8),
    .sel(Read_Address_2_rt));  // open: en
endmodule

module _16bit_Register_File (
  input  [15:0] DAta_In,
  input  [3:0] Read_Address_1_rs,
  input  [3:0] Read_Address_2_rt,
  input  [3:0] Data_Address__rd,
  input  Register_Weite,
  input  Clock,
  output [15:0] out_7,
  output [15:0] out_8
);

  wire and_1_out, and_2_out, and_3_out, and_4_out, and_5_out, and_6_out, and_7_out, and_8_out, and_9_out,
       and_10_out, and_11_out, and_12_out, and_13_out, and_14_out, and_15_out, and_16_out, decoder_1_out0,
       decoder_1_out1, decoder_1_out2, decoder_1_out3, decoder_1_out4, decoder_1_out5, decoder_1_out6,
       decoder_1_out7, decoder_1_out8, decoder_1_out9, decoder_1_out10, decoder_1_out11, decoder_1_out12,
       decoder_1_out13, decoder_1_out14, decoder_1_out15;
  wire [15:0] register_1_q, register_2_q, register_3_q, register_4_q, register_5_q, register_6_q,
       register_7_q, register_8_q, register_9_q, register_10_q, register_11_q, register_12_q, register_13_q,
       register_14_q, register_15_q, register_16_q;

  Decoder #(.select(4)) decoder_1 (
    .out0(decoder_1_out0), .out1(decoder_1_out1), .out2(decoder_1_out2), .out3(decoder_1_out3),
    .out4(decoder_1_out4), .out5(decoder_1_out5), .out6(decoder_1_out6), .out7(decoder_1_out7),
    .out8(decoder_1_out8), .out9(decoder_1_out9), .out10(decoder_1_out10), .out11(decoder_1_out11),
    .out12(decoder_1_out12), .out13(decoder_1_out13), .out14(decoder_1_out14), .out15(decoder_1_out15),
    .sel(Data_Address__rd));  // open: en
  and and_1 (and_1_out, decoder_1_out0, Register_Weite);
  and and_2 (and_2_out, decoder_1_out1, Register_Weite);
  and and_3 (and_3_out, decoder_1_out2, Register_Weite);
  and and_4 (and_4_out, decoder_1_out3, Register_Weite);
  and and_5 (and_5_out, decoder_1_out4, Register_Weite);
  and and_6 (and_6_out, decoder_1_out5, Register_Weite);
  and and_7 (and_7_out, decoder_1_out6, Register_Weite);
  and and_8 (and_8_out, decoder_1_out7, Register_Weite);
  and and_9 (and_9_out, decoder_1_out8, Register_Weite);
  and and_10 (and_10_out, decoder_1_out9, Register_Weite);
  and and_11 (and_11_out, decoder_1_out10, Register_Weite);
  and and_12 (and_12_out, decoder_1_out11, Register_Weite);
  and and_13 (and_13_out, decoder_1_out12, Register_Weite);
  and and_14 (and_14_out, decoder_1_out13, Register_Weite);
  and and_15 (and_15_out, decoder_1_out14, Register_Weite);
  and and_16 (and_16_out, decoder_1_out15, Register_Weite);
  Register #(.width(16)) register_1 (.D(DAta_In), .en(and_1_out), .Q(register_1_q), .clk(Clock));  // open: clr
  Register #(.width(16)) register_2 (.D(DAta_In), .en(and_2_out), .Q(register_2_q), .clk(Clock));  // open: clr
  Register #(.width(16)) register_3 (.D(DAta_In), .en(and_3_out), .Q(register_3_q), .clk(Clock));  // open: clr
  Register #(.width(16)) register_4 (.D(DAta_In), .en(and_4_out), .Q(register_4_q), .clk(Clock));  // open: clr
  Register #(.width(16)) register_5 (.D(DAta_In), .en(and_5_out), .Q(register_5_q), .clk(Clock));  // open: clr
  Register #(.width(16)) register_6 (.D(DAta_In), .en(and_6_out), .Q(register_6_q), .clk(Clock));  // open: clr
  Register #(.width(16)) register_7 (.D(DAta_In), .en(and_7_out), .Q(register_7_q), .clk(Clock));  // open: clr
  Register #(.width(16)) register_8 (.D(DAta_In), .en(and_8_out), .Q(register_8_q), .clk(Clock));  // open: clr
  Register #(.width(16)) register_9 (.D(DAta_In), .en(and_9_out), .Q(register_9_q), .clk(Clock));  // open: clr
  Register #(.width(16)) register_10 (.D(DAta_In), .en(and_10_out), .Q(register_10_q), .clk(Clock));  // open: clr
  Register #(.width(16)) register_11 (.D(DAta_In), .en(and_11_out), .Q(register_11_q), .clk(Clock));  // open: clr
  Register #(.width(16)) register_12 (.D(DAta_In), .en(and_12_out), .Q(register_12_q), .clk(Clock));  // open: clr
  Register #(.width(16)) register_13 (.D(DAta_In), .en(and_13_out), .Q(register_13_q), .clk(Clock));  // open: clr
  Register #(.width(16)) register_14 (.D(DAta_In), .en(and_14_out), .Q(register_14_q), .clk(Clock));  // open: clr
  Register #(.width(16)) register_15 (.D(DAta_In), .en(and_15_out), .Q(register_15_q), .clk(Clock));  // open: clr
  Register #(.width(16)) register_16 (.D(DAta_In), .en(and_16_out), .Q(register_16_q), .clk(Clock));  // open: clr
  Multiplexer #(.select(4), .width(16)) multiplexer_1 (
    .in0(register_1_q), .in1(register_2_q), .in2(register_3_q), .in3(register_4_q), .in4(register_5_q),
    .in5(register_6_q), .in6(register_7_q), .in7(register_8_q), .in8(register_9_q), .in9(register_10_q),
    .in10(register_11_q), .in11(register_12_q), .in12(register_13_q), .in13(register_14_q),
    .in14(register_15_q), .in15(register_16_q), .out(out_7), .sel(Read_Address_1_rs));  // open: en
  Multiplexer #(.select(4), .width(16)) multiplexer_2 (
    .in0(register_1_q), .in1(register_2_q), .in2(register_3_q), .in3(register_4_q), .in4(register_5_q),
    .in5(register_6_q), .in6(register_7_q), .in7(register_8_q), .in8(register_9_q), .in9(register_10_q),
    .in10(register_11_q), .in11(register_12_q), .in12(register_13_q), .in13(register_14_q),
    .in14(register_15_q), .in15(register_16_q), .out(out_8), .sel(Read_Address_2_rt));  // open: en
endmodule
